// Logisim project new.circ as structural Verilog: 7 circuits, main circuit main
module main (
  input  in_1,
  output [31:0] Instr,
  output RegWrite,
  output [4:0] RegAddr,
  output [31:0] RegData,
  output MemWrite,
  output [4:0] MemAddr,
  output [31:0] MemData
);

  wire aluB, clk, ifBeq, neqz, regSlt, toReg;
  wire [1:0] aluOp, extOp;
  wire [4:0] rd, rs, rt;
  wire [15:0] imm;
  wire [31:0] ALUres, dm_1_out, ext_1_output, grf_1_rd1, multiplexer_2_out;

  Clock clock_1 (.out(clk));
  // Probe on Instr
  controller controller_1 (
    .instr(Instr), .regSlt(regSlt), .regWE(RegWrite), .dmWE(MemWrite), .extOp(extOp), .aluOp(aluOp),
    .aluB(aluB), .toReg(toReg), .ifBeq(ifBeq), .rs(rs), .rt(rt), .rd(rd), .imm(imm));
  IFU ifu_1 (.in_1(ifBeq), .in_2(neqz), .in_3(in_1), .in_4(clk), .out_5(Instr));
  Multiplexer #(.width(5), .enable("false")) multiplexer_1 (.in0(rt), .in1(rd), .out(RegAddr), .sel(regSlt));
  grf grf_1 (
    .RA1(rs), .WA(RegAddr), .RegWrite(RegWrite), .WD(RegData), .RA2(rt), .Reset(in_1), .clk(clk),
    .RD1(grf_1_rd1), .RD2(MemData));
  EXT ext_1 (.\input (imm), .sel_00_0ext_01_signext_10_ext___0_2__11_toHigh16(extOp), .\output (ext_1_output));
  Multiplexer #(.width(32), .enable("false")) multiplexer_2 (
    .in0(MemData), .in1(ext_1_output), .out(multiplexer_2_out), .sel(aluB));
  alu alu_1 (
    .A(grf_1_rd1), .B(multiplexer_2_out), .sel_00__01__10__11(aluOp),
    .C({ALUres[31:7], MemAddr, ALUres[1:0]}), .notzero(neqz));
  DM dm_1 (.address(MemAddr), .data(MemData), .WE(MemWrite), .clk(clk), .reset(in_1), .out(dm_1_out));
  Multiplexer #(.width(32), .enable("false")) multiplexer_3 (
    .in0(dm_1_out), .in1({ALUres[31:7], MemAddr, ALUres[1:0]}), .out(RegData), .sel(toReg));

  // Other names for the same wires on the sheet: ALUres[6:2] = MemAddr; Data[31:0] = RegData; dmWE = MemWrite;
  //   readRt[31:0] = MemData; regWE = RegWrite; reset = in_1
endmodule

// ALU
module alu (
  input  [31:0] A,
  input  [31:0] B,
  input  [1:0] sel_00__01__10__11,
  output [31:0] C,
  output notzero
);

  wire [31:0] adder_1_out, and_1_out, or_1_out, subtractor_1_out;

  Adder #(.width(32)) adder_1 (.a(A), .b(B), .out(adder_1_out));  // open: cin, cout
  Subtractor #(.width(32)) subtractor_1 (.a(A), .b(B), .out(subtractor_1_out));  // open: bin, bout
  assign and_1_out = A & B;  // AND_Gate and_1, 32 bits wide
  assign or_1_out = A | B;  // OR_Gate or_1, 32 bits wide
  Multiplexer #(.select(2), .width(32), .enable("false")) multiplexer_1 (
    .in0(adder_1_out), .in1(subtractor_1_out), .in2(and_1_out), .in3(or_1_out), .out(C),
    .sel(sel_00__01__10__11));
  or or_2 (notzero, C[0], C[1], C[2], C[3], C[4], C[5], C[6], C[7], C[8], C[9], C[10], C[11], C[12], C[13], C[14], C[15], C[17], C[18], C[19], C[20], C[21], C[22], C[23], C[24], C[25], C[26], C[27], C[28], C[29], C[30], C[31]);
endmodule

// GRF
module grf (
  input  [4:0] RA1,
  input  [4:0] WA,
  input  RegWrite,
  input  [31:0] WD,
  input  [4:0] RA2,
  input  Reset,
  input  clk,
  output [31:0] RD1,
  output [31:0] RD2
);

  wire and_1_out, and_2_out, and_3_out, and_4_out, and_5_out, and_6_out, and_7_out, and_8_out, and_9_out,
       and_10_out, and_11_out, and_12_out, and_13_out, and_14_out, and_15_out, and_16_out, and_17_out,
       and_18_out, and_19_out, and_20_out, and_21_out, and_22_out, and_23_out, and_24_out, and_25_out,
       and_26_out, and_27_out, and_28_out, and_29_out, and_30_out, and_31_out, in1, in2, in3, in4, in5, in6,
       in7, in8, in9, in10, in11, in12, in13, in14, in15, in16, in17, in18, in19, in20, in21, in22, in23,
       in24, in25, in26, in27, in28, in29, in30, in31;
  wire [31:0] out1, out2, out3, out4, out5, out6, out7, out8, out9, out10, out11, out12, out13, out14, out15,
       out16, out17, out18, out19, out20, out21, out22, out23, out24, out25, out26, out27, out28, out29,
       out30, out31;

  Decoder #(.select(5)) decoder_1 (
    .out1(in1), .out2(in2), .out3(in3), .out4(in4), .out5(in5), .out6(in6), .out7(in7), .out8(in8),
    .out9(in9), .out10(in10), .out11(in11), .out12(in12), .out13(in13), .out14(in14), .out15(in15),
    .out16(in16), .out17(in17), .out18(in18), .out19(in19), .out20(in20), .out21(in21), .out22(in22),
    .out23(in23), .out24(in24), .out25(in25), .out26(in26), .out27(in27), .out28(in28), .out29(in29),
    .out30(in30), .out31(in31), .sel(WA));  // open: out0, en
  and and_1 (and_1_out, RegWrite, in4);
  and and_2 (and_2_out, RegWrite, in8);
  and and_3 (and_3_out, RegWrite, in12);
  and and_4 (and_4_out, RegWrite, in16);
  and and_5 (and_5_out, RegWrite, in20);
  and and_6 (and_6_out, RegWrite, in24);
  and and_7 (and_7_out, RegWrite, in28);
  Register #(.width(32)) register_1 (.D(WD), .en(and_1_out), .Q(out4), .clk(clk), .clr(Reset));
  Register #(.width(32)) register_2 (.D(WD), .en(and_2_out), .Q(out8), .clk(clk), .clr(Reset));
  Register #(.width(32)) register_3 (.D(WD), .en(and_3_out), .Q(out12), .clk(clk), .clr(Reset));
  Register #(.width(32)) register_4 (.D(WD), .en(and_4_out), .Q(out16), .clk(clk), .clr(Reset));
  Register #(.width(32)) register_5 (.D(WD), .en(and_5_out), .Q(out20), .clk(clk), .clr(Reset));
  Register #(.width(32)) register_6 (.D(WD), .en(and_6_out), .Q(out24), .clk(clk), .clr(Reset));
  Register #(.width(32)) register_7 (.D(WD), .en(and_7_out), .Q(out28), .clk(clk), .clr(Reset));
  Multiplexer #(.select(5), .width(32)) multiplexer_1 (
    .in0({32{1'b0}}), .in1(out1), .in2(out2), .in3(out3), .in4(out4), .in5(out5), .in6(out6), .in7(out7),
    .in8(out8), .in9(out9), .in10(out10), .in11(out11), .in12(out12), .in13(out13), .in14(out14),
    .in15(out15), .in16(out16), .in17(out17), .in18(out18), .in19(out19), .in20(out20), .in21(out21),
    .in22(out22), .in23(out23), .in24(out24), .in25(out25), .in26(out26), .in27(out27), .in28(out28),
    .in29(out29), .in30(out30), .in31(out31), .out(RD1), .sel(RA1));  // open: en
  and and_8 (and_8_out, RegWrite, in1);
  and and_9 (and_9_out, RegWrite, in5);
  and and_10 (and_10_out, RegWrite, in9);
  and and_11 (and_11_out, RegWrite, in13);
  and and_12 (and_12_out, RegWrite, in17);
  and and_13 (and_13_out, RegWrite, in21);
  and and_14 (and_14_out, RegWrite, in25);
  and and_15 (and_15_out, RegWrite, in29);
  Register #(.width(32)) register_8 (.D(WD), .en(and_8_out), .Q(out1), .clk(clk), .clr(Reset));
  Register #(.width(32)) register_9 (.D(WD), .en(and_9_out), .Q(out5), .clk(clk), .clr(Reset));
  Register #(.width(32)) register_10 (.D(WD), .en(and_10_out), .Q(out9), .clk(clk), .clr(Reset));
  Register #(.width(32)) register_11 (.D(WD), .en(and_11_out), .Q(out13), .clk(clk), .clr(Reset));
  Register #(.width(32)) register_12 (.D(WD), .en(and_12_out), .Q(out17), .clk(clk), .clr(Reset));
  Register #(.width(32)) register_13 (.D(WD), .en(and_13_out), .Q(out21), .clk(clk), .clr(Reset));
  Register #(.width(32)) register_14 (.D(WD), .en(and_14_out), .Q(out25), .clk(clk), .clr(Reset));
  Register #(.width(32)) register_15 (.D(WD), .en(and_15_out), .Q(out29), .clk(clk), .clr(Reset));
  and and_16 (and_16_out, RegWrite, in2);
  and and_17 (and_17_out, RegWrite, in14);
  and and_18 (and_18_out, RegWrite, in18);
  Register #(.width(32)) register_16 (.D(WD), .en(and_16_out), .Q(out2), .clk(clk), .clr(Reset));
  Register #(.width(32)) register_17 (.D(WD), .en(and_19_out), .Q(out6), .clk(clk), .clr(Reset));
  and and_19 (and_19_out, RegWrite, in6);
  Register #(.width(32)) register_18 (.D(WD), .en(and_20_out), .Q(out10), .clk(clk), .clr(Reset));
  and and_20 (and_20_out, RegWrite, in10);
  Register #(.width(32)) register_19 (.D(WD), .en(and_17_out), .Q(out14), .clk(clk), .clr(Reset));
  Register #(.width(32)) register_20 (.D(WD), .en(and_18_out), .Q(out18), .clk(clk), .clr(Reset));
  Register #(.width(32)) register_21 (.D(WD), .en(and_21_out), .Q(out22), .clk(clk), .clr(Reset));
  and and_21 (and_21_out, RegWrite, in22);
  Register #(.width(32)) register_22 (.D(WD), .en(and_22_out), .Q(out26), .clk(clk), .clr(Reset));
  and and_22 (and_22_out, RegWrite, in26);
  Register #(.width(32)) register_23 (.D(WD), .en(and_23_out), .Q(out30), .clk(clk), .clr(Reset));
  and and_23 (and_23_out, RegWrite, in30);
  Multiplexer #(.select(5), .width(32)) multiplexer_2 (
    .in0({32{1'b0}}), .in1(out1), .in2(out2), .in3(out3), .in4(out4), .in5(out5), .in6(out6), .in7(out7),
    .in8(out8), .in9(out9), .in10(out10), .in11(out11), .in12(out12), .in13(out13), .in14(out14),
    .in15(out15), .in16(out16), .in17(out17), .in18(out18), .in19(out19), .in20(out20), .in21(out21),
    .in22(out22), .in23(out23), .in24(out24), .in25(out25), .in26(out26), .in27(out27), .in28(out28),
    .in29(out29), .in30(out30), .in31(out31), .out(RD2), .sel(RA2));  // open: en
  and and_24 (and_24_out, RegWrite, in3);
  and and_25 (and_25_out, RegWrite, in7);
  and and_26 (and_26_out, RegWrite, in11);
  and and_27 (and_27_out, RegWrite, in15);
  and and_28 (and_28_out, RegWrite, in19);
  and and_29 (and_29_out, RegWrite, in23);
  and and_30 (and_30_out, RegWrite, in27);
  and and_31 (and_31_out, RegWrite, in31);
  Register #(.width(32)) register_24 (.D(WD), .en(and_24_out), .Q(out3), .clk(clk), .clr(Reset));
  Register #(.width(32)) register_25 (.D(WD), .en(and_25_out), .Q(out7), .clk(clk), .clr(Reset));
  Register #(.width(32)) register_26 (.D(WD), .en(and_26_out), .Q(out11), .clk(clk), .clr(Reset));
  Register #(.width(32)) register_27 (.D(WD), .en(and_27_out), .Q(out15), .clk(clk), .clr(Reset));
  Register #(.width(32)) register_28 (.D(WD), .en(and_28_out), .Q(out19), .clk(clk), .clr(Reset));
  Register #(.width(32)) register_29 (.D(WD), .en(and_29_out), .Q(out23), .clk(clk), .clr(Reset));
  Register #(.width(32)) register_30 (.D(WD), .en(and_30_out), .Q(out27), .clk(clk), .clr(Reset));
  Register #(.width(32)) register_31 (.D(WD), .en(and_31_out), .Q(out31), .clk(clk), .clr(Reset));

  // Other names for the same wires on the sheet: WE = RegWrite
endmodule

module IFU (
  input  in_1,
  input  in_2,
  input  in_3,
  input  in_4,
  output [31:0] out_5
);

  wire and_1_out, not_1_out, register_1_q;
  wire [31:0] adder_1_out, ext_1_output, lpc, multiplexer_1_out, multiplexer_2_out, pc;

  EXT ext_1 (.\input (out_5[15:0]), .sel_00_0ext_01_signext_10_ext___0_2__11_toHigh16(2'b10), .\output (ext_1_output));
  not not_1 (not_1_out, in_2);
  Multiplexer #(.width(32), .enable("false")) multiplexer_1 (
    .in0({32{1'b0}}), .in1(pc), .out(multiplexer_1_out), .sel(register_1_q));
  Register #(.width(1)) register_1 (.D(1'b1), .Q(register_1_q), .clk(in_4), .clr(in_3));  // open: en
  Multiplexer #(.width(32), .enable("false")) multiplexer_2 (
    .in0({32{1'b0}}), .in1(ext_1_output), .out(multiplexer_2_out), .sel(and_1_out));
  and and_1 (and_1_out, in_1, not_1_out);
  Register #(.width(32)) register_2 (.D(multiplexer_1_out), .Q(lpc), .clk(in_4), .clr(in_3));  // open: en
  Adder #(.width(32)) adder_1 (.a(lpc), .b(32'h4), .out(adder_1_out));  // open: cin, cout
  Adder #(.width(32)) adder_2 (.a(adder_1_out), .b(multiplexer_2_out), .out(pc));  // open: cin, cout
  // Probe on pc
  ROM #(.addrWidth(5), .dataWidth(32)) rom_1 (.addr(lpc[6:2]), .data(out_5));  // open: sel

  // Other names for the same wires on the sheet: clk = in_4; ifBeq = in_1; instr[31:0] = out_5; neqz = in_2;
  //   reset = in_3

  // Notes on the sheet:
  //   contents of rom_1 (hex, n*v repeats v):
  //   35080000 3529000a 354a0000 11090009 1495021 3c010000 34210001 1014021 3c010000 34210004 1615821
  //   ad6a0000 1108fff6
endmodule

module EXT (
  input  [15:0] \input ,
  input  [1:0] sel_00_0ext_01_signext_10_ext___0_2__11_toHigh16,
  output [31:0] \output 
);

  Multiplexer #(.select(2), .width(32), .enable("false")) multiplexer_1 (
    .in0({{16{1'b0}}, \input }), .in1({{17{\input [15]}}, \input [14:0]}),
    .in2({{15{\input [15]}}, \input [14:0], 2'b00}), .in3({\input , {16{1'b0}}}), .out(\output ),
    .sel(sel_00_0ext_01_signext_10_ext___0_2__11_toHigh16));

  // Other names for the same wires on the sheet: sel[1:0] = sel_00_0ext_01_signext_10_ext___0_2__11_toHigh16;
  //   _2_signext[31:2] = {{15{\input [15]}}, \input [14:0]}; in[15:0] = \input ;
  //   signext[31:0] = {{17{\input [15]}}, \input [14:0]}; tohigh[31:16] = \input ; zeroext[15:0] = \input ;
  //   sign = \input [15]
endmodule

module DM (
  input  [4:0] address,
  input  [31:0] data,
  input  WE,
  input  clk,
  input  reset,
  output [31:0] out
);

  RAM #(.addrWidth(5), .dataWidth(32), .bus("separate")) ram_1 (
    .addr(address), .din(data), .data(out), .str(WE), .clk(clk), .clr(reset));  // open: sel, ld
endmodule

// CTL
module controller (
  input  [31:0] instr,
  output regSlt,
  output regWE,
  output dmWE,
  output [1:0] extOp,
  output [1:0] aluOp,
  output aluB,
  output toReg,
  output ifBeq,
  output [4:0] rs,
  output [4:0] rt,
  output [4:0] rd,
  output [15:0] imm
);

  wire addu, lui, lw, not_1_out, not_2_out, not_3_out, not_4_out, not_5_out, not_6_out, not_7_out, not_8_out,
       not_9_out, not_10_out, not_11_out, not_12_out, subu;

  not not_1 (not_1_out, instr[30]);
  not not_2 (not_2_out, instr[31]);
  not not_3 (not_3_out, instr[29]);
  not not_4 (not_4_out, instr[28]);
  not not_5 (not_5_out, instr[27]);
  not not_6 (not_6_out, instr[26]);
  not not_7 (not_7_out, instr[5]);
  not not_8 (not_8_out, instr[4]);
  not not_9 (not_9_out, instr[3]);
  not not_10 (not_10_out, instr[1]);
  not not_11 (not_11_out, instr[2]);
  not not_12 (not_12_out, instr[0]);
  and u_addu (addu, not_2_out, not_1_out, not_3_out, not_4_out, not_5_out, not_6_out, instr[5], not_8_out, not_9_out, not_11_out, not_10_out, instr[0]);
  and u_subu (subu, not_2_out, not_1_out, not_3_out, not_4_out, not_5_out, not_6_out, instr[5], not_8_out, not_9_out, not_11_out, instr[1], instr[0]);
  and ori (aluOp[1], not_2_out, not_1_out, instr[29], instr[28], not_5_out, instr[26]);
  and u_lw (lw, instr[31], not_1_out, not_3_out, not_4_out, instr[27], instr[26]);
  and sw (dmWE, instr[31], not_1_out, instr[29], not_4_out, instr[27], instr[26]);
  and u_lui (lui, not_2_out, not_1_out, instr[29], instr[28], instr[27], instr[26]);
  and beq (ifBeq, not_2_out, not_1_out, not_3_out, instr[28], not_5_out, not_6_out);
  or or_1 (regSlt, addu, subu);
  or or_2 (regWE, addu, subu, aluOp[1], lw, lui);
  or or_3 (toReg, addu, subu, aluOp[1], lui);
  or or_4 (aluOp[0], aluOp[1], ifBeq, subu);
  or or_5 (extOp[0], dmWE, lw, lui);
  or or_6 (extOp[1], ifBeq, lui);
  or or_7 (aluB, dmWE, lw, lui, aluOp[1]);

  assign imm = instr[15:0];
  assign rd = instr[15:11];
  assign rs = instr[25:21];
  assign rt = instr[20:16];

  // Other names for the same wires on the sheet: ori = aluOp[1]; beq = ifBeq; func[5:0] = instr[5:0];
  //   sha[4:0] = instr[10:6]; op[5:0] = instr[31:26]; sw = dmWE

  // Notes on the sheet:
  //   0:rt,1:rd
endmodule
